# Fritzing sketch MotorRig (saved by Fritzing 1.0.1rc)
breadboards: 1

parts:
  STM32_F446RE = STM32 Nucleo boards
  H-bridge_power_stage = BTS7960
  ACS712 = Current Sensor 5A
  12V_DC_adapter = Screw terminal - 2 pins [package=THT]
  DC_motor = DC Motor with two-phase hall-encoder
  R3 = Resistor [tolerance=±5% resistance=10000 package="1206 [SMD]"]
  R4 = Resistor [tolerance=±5% resistance=10000 package="1206 [SMD]"]

nets:
  N1: STM32_F446RE.A0, H-bridge_power_stage.pin1
  N2: STM32_F446RE.A1, H-bridge_power_stage.pin2
  N3: STM32_F446RE.A2, R3.Pin_0, R4.Pin_0
  N4: STM32_F446RE.A3, H-bridge_power_stage.pin3
  N5: STM32_F446RE.D11_PWM/MOSI, DC_motor.pin4
  N6: STM32_F446RE.D12/MISO, DC_motor.pin3
  N7: STM32_F446RE.D4, H-bridge_power_stage.pin4
  N8: STM32_F446RE.3V3, DC_motor.pin5
  5V: STM32_F446RE.5V, H-bridge_power_stage.pin7, ACS712.VCC
  GND: STM32_F446RE.GND, H-bridge_power_stage.pin8, ACS712.GND, DC_motor.pin2, R4.Pin_1
  N9: H-bridge_power_stage.pin9, ACS712.2, ACS712.OUT, R3.Pin_1
  N10: H-bridge_power_stage.pin10, DC_motor.pin6
  N11: H-bridge_power_stage.pin11, 12V_DC_adapter.pin2
  N12: H-bridge_power_stage.pin12, 12V_DC_adapter.pin1
  N13: ACS712.1, DC_motor.pin1

custom parts:
  BTS7960: BTS7960 43A Peak Power H-Bridge PWM Motor Driver
